# Fritzing sketch pcb - top + bottom (saved by Fritzing 0.9.2b)
breadboards: 1

parts:
  JP_top_+5V0_DC = Header 1 [package=1x01_offset]
  JP_top_V_rect = Header 1 [package=1x01_offset]
  JP_top_V_test = Header 1 [package=1x01_offset]
  JP_top_neg_02 = Header 1 [package=1x01_offset]
  JP_top_neg_01 = Header 1 [package=1x01_offset]
  top_5V0_DC_out = Header 2 [package=molex-1x2_lock]
  330μ1 = Capacitor Polarized [package=panasonic_g]
  22μ1 = Capacitor Polarized [package=panasonic_d]
  1N4148 = Diode [package=diode-1n4001]
  BZG03C24 = Zener Diode [part_number=1N4732A breakdown_voltage=3.6V package="Melf DO-213 AB [SMD]"]
  BZG03C24_2 = Zener Diode [part_number=1N4732A breakdown_voltage=3.6V package="Melf DO-213 AB [SMD]"]
  JPbottom_neg_02 = Header 1 [package=1x01_offset]
  bottom_AC_in = Header 2 [package=molex-1x2_lock]
  JP_top_+5V0_DC_2 = Header 1 [package=1x01_offset]
  JP_bottom_V_rect = Header 1 [package=1x01_offset]
  JP_bottom_V_test = Header 1 [package=1x01_offset]
  JP_bottom_neg_01 = Header 1 [package=1x01_offset]
  Recom_R-78B5_0-1_1 = Voltage Regulator [package=to-220-alt]
  1N4149 = Diode [package=diode-1n4001]
  IRF7319_1 = SO08-EIAJ [chip_label=IRF7319 package=SO]  # not connected
  IRF7319_2 = SO08-EIAJ [chip_label=IRF7319 package=SO]  # not connected

nets:
  5V0 DC: JP_top_+5V0_DC.1, top_5V0_DC_out.1, 22μ1.+, 1N4148.A, JP_top_+5V0_DC_2.1, Recom_R-78B5_0-1_1.OUT
  V rect: JP_top_V_rect.1, JP_bottom_V_rect.1, 1N4149.A
  V test: JP_top_V_test.1, JP_bottom_V_test.1
  top GND: JP_top_neg_02.1, JP_top_neg_01.1, top_5V0_DC_out.2
  N1: 330μ1.+, 1N4148.C, Recom_R-78B5_0-1_1.IN, 1N4149.C
  GND/bottom GND: 330μ1.-, 22μ1.-, JPbottom_neg_02.1, JP_bottom_neg_01.1, Recom_R-78B5_0-1_1.GND
  N2: BZG03C24.cathode, BZG03C24_2.cathode
  AC_in_0: BZG03C24.anode, bottom_AC_in.2
  AC_in_1: BZG03C24_2.anode, bottom_AC_in.1

notes:
  +
  ~
  -
  down
  IRF7319
  bottom
  čos
  up
  top
  hrvoje ivanic
  2016
  bottom pcb
  top pcb
